// Logisim project circuit1c.circ as structural Verilog: 1 circuit, main circuit main
module main (
  input  A,
  input  B,
  input  C,
  output out1,
  output out2
);

  wire and_1_out, not_1_out, not_2_out, or_1_out, or_2_out;

  or or_1 (or_1_out, B, C);
  not not_1 (not_1_out, or_1_out);
  or or_2 (or_2_out, or_1_out, A);
  and and_1 (and_1_out, C, B);
  and and_2 (out1, A, not_1_out);
  not not_2 (not_2_out, or_2_out);
  or or_3 (out2, not_2_out, and_1_out);
endmodule
