// Logisim project ignition.circ as structural Verilog: 1 circuit, main circuit main
module main (
  input  start_engine,
  input  engine_running,
  output starter_motor,
  output ignition_coil
);

  wire and_1_out, and_2_out, and_3_out, and_4_out, and_6_out, and_7_out, and_8_out, clock_1_out, d0, d1,
       not_1_out, not_2_out, notq0, notq1, or_1_out, or_2_out, or_4_out, q0, q1;

  Clock clock_1 (.out(clock_1_out));
  D_Flip_Flop u_d0 (.D(d0), .clk(clock_1_out), .Q(q0), .Qn(notq0));  // open: preset, reset
  D_Flip_Flop u_d1 (.D(d1), .clk(clock_1_out), .Q(q1), .Qn(notq1));  // open: preset, reset
  not not_1 (not_1_out, engine_running);
  or or_1 (or_1_out, start_engine, engine_running);
  and and_1 (and_1_out, notq0, notq1, start_engine);
  or or_2 (or_2_out, start_engine, not_1_out);
  and and_2 (and_2_out, q1, notq0, start_engine, engine_running);
  and and_3 (and_3_out, q1, q0, or_1_out);
  and and_4 (and_4_out, notq1, q0, or_2_out);
  or or_3 (d0, and_1_out, and_4_out, and_2_out, and_3_out);
  not not_2 (not_2_out, start_engine);
  or or_4 (or_4_out, start_engine, engine_running);
  and and_5 (starter_motor, notq1, q0);
  and and_6 (and_6_out, notq1, q0, not_2_out, engine_running);
  and and_7 (and_7_out, q1, notq0, engine_running);
  and and_8 (and_8_out, q1, q0, or_4_out);
  xor xor_1 (ignition_coil, q1, q0);
  or or_5 (d1, and_6_out, and_7_out, and_8_out);

  // Other names for the same wires on the sheet: IC = ignition_coil; In_ER = engine_running; In_SE = start_engine;
  //   SM = starter_motor
endmodule
