// Logisim project my_adder.circ as structural Verilog: 1 circuit, main circuit main
module main (
  input  [15:0] A,
  input  [15:0] B
);


  // Other names for the same wires on the sheet: b0 = A[0]; b1 = A[1]; b2 = A[2]; b3 = A[3]; b4 = A[4]; b5 = A[5];
  //   b6 = A[6]; b7 = A[7]; b8 = A[8]; b9 = A[9]
endmodule
